# Fritzing sketch Circuit Diagram (saved by Fritzing 0.9.3b)

parts:
  Part2 = GY-VL53L0XV2 Laser Ranger Module
  WeMos_D1_Mini1 = WeMos D1 Mini
  LCD1 = LCD screen
  J1 = Piezo Speaker

nets:
  VCC: Part2.VCC, WeMos_D1_Mini1.3V3
  N1: Part2.GND, WeMos_D1_Mini1.G, J1.pin1
  N2: Part2.SCL, WeMos_D1_Mini1.D1
  N3: Part2.SDA, WeMos_D1_Mini1.D2
  N4: WeMos_D1_Mini1.D0, LCD1.E
  N5: WeMos_D1_Mini1.D3, LCD1.RS
  N6: WeMos_D1_Mini1.D4, J1.pin2
  N7: WeMos_D1_Mini1.D5, LCD1.DB4
  N8: WeMos_D1_Mini1.D6, LCD1.DB5
  N9: WeMos_D1_Mini1.D7, LCD1.DB6
  N10: WeMos_D1_Mini1.D8, LCD1.DB7

custom parts:
  GY-VL53L0XV2 Laser Ranger Module: The GY-VL53L0XV2 is based on the VL53L0X from ST Microelectronics, a time-of-flight ranging system integrated into a compact module.
