# Fritzing sketch CircuitDiagram (saved by Fritzing 0.9.3b)

parts:
  Part2 = GY-VL53L0XV2 Laser Ranger Module
  WeMos_D1_Mini1 = WeMos D1 Mini
  LCD1 = LCD screen
  J1 = Piezo Speaker
  U1 = POT [package=pot_mammoth]
  R1 = Resistor [tolerance=±5% resistance=1k package="2010 [SMD]"]
  S1 = Pushbutton [package="[SMD]"]

nets:
  VCC: Part2.VCC, WeMos_D1_Mini1.3V3, R1.Pin_0
  GND: Part2.GND, WeMos_D1_Mini1.G, LCD1.VSS, LCD1.R/W, LCD1.LED-, J1.pin1, U1.S, S1.Pin_1, S1.Pin_2
  N1: Part2.SCL, WeMos_D1_Mini1.D1
  N2: Part2.SDA, WeMos_D1_Mini1.D2
  5V: WeMos_D1_Mini1.5V, LCD1.VDD, U1.E
  N3: WeMos_D1_Mini1.D0, LCD1.E
  N4: WeMos_D1_Mini1.D3, LCD1.RS
  N5: WeMos_D1_Mini1.D4, J1.pin2
  N6: WeMos_D1_Mini1.D5, LCD1.DB4
  N7: WeMos_D1_Mini1.D6, LCD1.DB5
  N8: WeMos_D1_Mini1.D7, LCD1.DB6
  N9: WeMos_D1_Mini1.D8, LCD1.DB7
  N10: WeMos_D1_Mini1.RST, S1.Pin_3, S1.Pin_4
  N11: LCD1.V0, U1.A
  N12: LCD1.LED+, R1.Pin_1

custom parts:
  GY-VL53L0XV2 Laser Ranger Module: The GY-VL53L0XV2 is based on the VL53L0X from ST Microelectronics, a time-of-flight ranging system integrated into a compact module.
